// Logisim project Clock.circ as structural Verilog: 5 circuits, main circuit main
module main (
);

  wire and_1_out, and_2_out, and_3_out, and_4_out, and_5_out, and_6_out, clock_1_out, or_1_out;
  wire [1:0] counter_div_2_1_q0;
  wire [2:0] counter_div_6_1_q0, counter_div_6_2_q0;
  wire [3:0] counter_div_10_1_q0, counter_div_10_2_q0, counter_div_input_1_q0;

  or or_1 (or_1_out, and_3_out, and_1_out);
  counter_div_2 counter_div_2_1 (
    .clock(clock_1_out), .pause(or_1_out), .Q0(counter_div_2_1_q0[0]), .Q1(counter_div_2_1_q0[1]));
  and and_1 (and_1_out, counter_div_input_1_q0[1], counter_div_input_1_q0[3]);
  Hex_Digit_Display hex_digit_display_1 (.value({2'b00, counter_div_2_1_q0}));  // open: dp
  counter_div_input counter_div_input_1 (
    .clock(clock_1_out), .pause(and_2_out), .Q0(counter_div_input_1_q0[0]), .Q1(counter_div_input_1_q0[1]),
    .Q2(counter_div_input_1_q0[2]), .Q3(counter_div_input_1_q0[3]), .reset_hour_2(and_3_out));
  and and_2 (and_2_out, counter_div_6_1_q0[1], counter_div_6_1_q0[2]);
  Hex_Digit_Display hex_digit_display_2 (.value(counter_div_input_1_q0));  // open: dp
  and and_3 (and_3_out, counter_div_2_1_q0[1], counter_div_input_1_q0[2]);
  LED led_1 (.in(1'b1));
  LED led_2 (.in(1'b1));
  Hex_Digit_Display hex_digit_display_3 (.value({1'b0, counter_div_6_1_q0}));  // open: dp
  counter_div_6 counter_div_6_1 (
    .clock(clock_1_out), .pause(and_4_out), .Q0(counter_div_6_1_q0[0]), .Q1(counter_div_6_1_q0[1]),
    .Q2(counter_div_6_1_q0[2]));
  and and_4 (and_4_out, counter_div_10_1_q0[1], counter_div_10_1_q0[3]);
  Hex_Digit_Display hex_digit_display_4 (.value(counter_div_10_1_q0));  // open: dp
  counter_div_10 counter_div_10_1 (
    .clock(clock_1_out), .pause(and_5_out), .Q0(counter_div_10_1_q0[0]), .Q1(counter_div_10_1_q0[1]),
    .Q2(counter_div_10_1_q0[2]), .Q3(counter_div_10_1_q0[3]));
  and and_5 (and_5_out, counter_div_6_2_q0[1], counter_div_6_2_q0[2]);
  LED led_3 (.in(1'b1));
  LED led_4 (.in(1'b1));
  Hex_Digit_Display hex_digit_display_5 (.value({1'b0, counter_div_6_2_q0}));  // open: dp
  Hex_Digit_Display hex_digit_display_6 (.value(counter_div_10_2_q0));  // open: dp
  counter_div_6 counter_div_6_2 (
    .clock(clock_1_out), .pause(and_6_out), .Q0(counter_div_6_2_q0[0]), .Q1(counter_div_6_2_q0[1]),
    .Q2(counter_div_6_2_q0[2]));
  and and_6 (and_6_out, counter_div_10_2_q0[1], counter_div_10_2_q0[3]);
  counter_div_10 counter_div_10_2 (
    .clock(clock_1_out), .pause(1'b1), .Q0(counter_div_10_2_q0[0]), .Q1(counter_div_10_2_q0[1]),
    .Q2(counter_div_10_2_q0[2]), .Q3(counter_div_10_2_q0[3]));
  Clock clock_1 (.out(clock_1_out));
endmodule

module counter_div_10 (
  input  clock,
  input  pause,
  output Q0,
  output Q1,
  output Q2,
  output Q3
);

  wire and_1_out, and_2_out, t_ff_1_qn, t_ff_2_qn, t_ff_3_qn;

  and and_1 (and_1_out, clock, pause);
  T_Flip_Flop t_ff_1 (.clk(and_1_out), .T(1'b1), .Q(Q0), .Qn(t_ff_1_qn), .reset(and_2_out));  // open: preset, en
  T_Flip_Flop t_ff_2 (.clk(t_ff_1_qn), .T(1'b1), .Q(Q1), .Qn(t_ff_2_qn), .reset(and_2_out));  // open: preset, en
  T_Flip_Flop t_ff_3 (.clk(t_ff_2_qn), .T(1'b1), .Q(Q2), .Qn(t_ff_3_qn), .reset(and_2_out));  // open: preset, en
  T_Flip_Flop t_ff_4 (.clk(t_ff_3_qn), .T(1'b1), .Q(Q3), .reset(and_2_out));  // open: Qn, preset, en
  and and_2 (and_2_out, Q3, Q1);
endmodule

module counter_div_6 (
  input  clock,
  input  pause,
  output Q0,
  output Q1,
  output Q2
);

  wire and_1_out, and_2_out, t_ff_1_qn, t_ff_2_qn;

  and and_1 (and_1_out, clock, pause);
  T_Flip_Flop t_ff_1 (.clk(and_1_out), .T(1'b1), .Q(Q0), .Qn(t_ff_1_qn), .reset(and_2_out));  // open: preset, en
  T_Flip_Flop t_ff_2 (.clk(t_ff_1_qn), .T(1'b1), .Q(Q1), .Qn(t_ff_2_qn), .reset(and_2_out));  // open: preset, en
  T_Flip_Flop t_ff_3 (.clk(t_ff_2_qn), .T(1'b1), .Q(Q2), .reset(and_2_out));  // open: Qn, preset, en
  and and_2 (and_2_out, Q2, Q1);
endmodule

module counter_div_2 (
  input  clock,
  input  pause,
  output Q0,
  output Q1
);

  wire and_1_out, and_2_out, t_ff_1_qn;

  and and_1 (and_1_out, clock, pause);
  T_Flip_Flop t_ff_1 (.clk(and_1_out), .T(1'b1), .Q(Q0), .Qn(t_ff_1_qn), .reset(and_2_out));  // open: preset, en
  T_Flip_Flop t_ff_2 (.clk(t_ff_1_qn), .T(1'b1), .Q(Q1), .reset(and_2_out));  // open: Qn, preset, en
  and and_2 (and_2_out, Q1, Q0);
endmodule

module counter_div_input (
  input  clock,
  input  pause,
  input  reset_hour_2,
  output Q0,
  output Q1,
  output Q2,
  output Q3
);

  wire and_1_out, and_2_out, or_1_out, t_ff_1_qn, t_ff_2_qn, t_ff_3_qn;

  and and_1 (and_1_out, clock, pause);
  T_Flip_Flop t_ff_1 (.clk(and_1_out), .T(1'b1), .Q(Q0), .Qn(t_ff_1_qn), .reset(or_1_out));  // open: preset, en
  T_Flip_Flop t_ff_2 (.clk(t_ff_1_qn), .T(1'b1), .Q(Q1), .Qn(t_ff_2_qn), .reset(or_1_out));  // open: preset, en
  T_Flip_Flop t_ff_3 (.clk(t_ff_2_qn), .T(1'b1), .Q(Q2), .Qn(t_ff_3_qn), .reset(or_1_out));  // open: preset, en
  T_Flip_Flop t_ff_4 (.clk(t_ff_3_qn), .T(1'b1), .Q(Q3), .reset(or_1_out));  // open: Qn, preset, en
  or or_1 (or_1_out, and_2_out, reset_hour_2);
  and and_2 (and_2_out, Q3, Q1);
endmodule
