// Logisim project counter_div_2.circ as structural Verilog: 1 circuit, main circuit main
module main (
  input  clock,
  input  pause,
  output Q0,
  output Q1
);

  wire and_1_out, and_2_out, t_ff_1_qn;

  and and_1 (and_1_out, clock, pause);
  T_Flip_Flop t_ff_1 (.clk(and_1_out), .T(1'b1), .Q(Q0), .Qn(t_ff_1_qn), .reset(and_2_out));  // open: preset, en
  T_Flip_Flop t_ff_2 (.clk(t_ff_1_qn), .T(1'b1), .Q(Q1), .reset(and_2_out));  // open: Qn, preset, en
  and and_2 (and_2_out, Q1, Q0);
endmodule
